// Logisim project CPU_t3.circ as structural Verilog: 7 circuits, main circuit main
module main (
  input  [31:0] in_1,
  input  in_2,
  input  in_3,
  input  in_4,
  input  [4:0] in_5,
  input  [4:0] in_6,
  input  [3:0] in_7,
  output [31:0] out_8,
  output [19:0] out_9
);

  wire adr_color, adr_kmt, adr_posx, adr_posy, and_1_out, and_2_out, and_3_out, and_4_out, and_5_out,
       and_6_out, and_7_out, and_8_out, CLK, comparator_1_lt, comparator_5_eq, comparator_6_eq,
       comparator_7_eq, comparator_8_eq, comparator_9_eq, comparator_10_eq, comparator_11_eq,
       comparator_12_eq, cpu_1_read, CPU_write, or_1_out, or_2_out, por_1_out, register_1_q, undriven;
  wire [0:0] bit_extender_1_out_2, bit_extender_2_out_2;
  wire [2:0] Flag_Reg, Posta_A, Posta_B;
  wire [3:0] bit_extender_2_out, rgb_video_1_p6;
  wire [4:0] rgb_video_1_p4, rgb_video_1_p5;
  wire [6:0] bitselector_3_out, controlled_buffer_4_out;
  wire [7:0] bit_extender_1_out;
  wire [7:5] bit_extender_2_out_3;
  wire [19:0] bitselector_1_out, controlled_buffer_1_out;
  wire [20:0] bitselector_4_out, register_2_q;
  wire [31:0] Command, controlled_buffer_2_out, cpu_1_outaddress, cpu_1_outdata, deb_adr, deb_r0, deb_r1,
       deb_r2, deb_r3, deb_r4, deb_r5, deb_r6, deb_r7, IR, MAR, MDR, PC, ram_1_dout;

  CPU cpu_1 (
    .CLK(CLK), .inData(out_8), .in_3(undriven), .outAddress(cpu_1_outaddress), .outData(cpu_1_outdata),
    .Read(cpu_1_read), .Write(CPU_write), .deb_PC(PC), .deb_MAR(MAR), .deb_IR(IR), .deb_MDR(MDR),
    .debFlagReg(Flag_Reg), .deb_posta_A(Posta_A), .deb_posta_B(Posta_B), .deb_r7(deb_r7), .deb_r6(deb_r6),
    .deb_r5(deb_r5), .deb_r4(deb_r4), .deb_r3(deb_r3), .deb_r2(deb_r2), .deb_r1(deb_r1), .deb_r0(deb_r0),
    .deb_AdrReg(deb_adr), .out_34(Command));  // open: in_4, in_5, in_6, in_7, in_8, in_9, in_10, in_11, in_12, debSP
  Comparator #(.mode("unsigned"), .width(32)) comparator_1 (
    .a(cpu_1_outaddress), .b(32'hfffffff8), .eq(adr_posy), .lt(comparator_1_lt));  // open: gt
  Comparator #(.mode("unsigned"), .width(32)) comparator_2 (
    .a(cpu_1_outaddress), .b(32'hfffffff9), .eq(adr_posx));  // open: gt, lt
  Comparator #(.mode("unsigned"), .width(32)) comparator_3 (
    .a(cpu_1_outaddress), .b(32'hfffffffa), .eq(adr_color));  // open: gt, lt
  Comparator #(.mode("unsigned"), .width(32)) comparator_4 (
    .a(cpu_1_outaddress), .b(32'hfffffffb), .eq(adr_kmt));  // open: gt, lt
  Comparator #(.mode("unsigned"), .width(32)) comparator_5 (
    .a(cpu_1_outaddress), .b(32'hfffffffc), .eq(comparator_5_eq));  // open: gt, lt
  Comparator #(.mode("unsigned"), .width(32)) comparator_6 (
    .a(cpu_1_outaddress), .b(32'hfffffffd), .eq(comparator_6_eq));  // open: gt, lt
  Comparator #(.mode("unsigned"), .width(32)) comparator_7 (
    .a(cpu_1_outaddress), .b(32'hfffffffe), .eq(comparator_7_eq));  // open: gt, lt
  Comparator #(.mode("unsigned"), .width(32)) comparator_8 (
    .a(cpu_1_outaddress), .b({32{1'b1}}), .eq(comparator_8_eq));  // open: gt, lt
  BitSelector #(.group(20), .width(32)) bitselector_1 (.in(cpu_1_outaddress), .out(bitselector_1_out), .sel(1'b0));
  Hex_Digit_Display hex_digit_display_1 (.value(PC[31:28]));  // open: dp
  Hex_Digit_Display hex_digit_display_2 (.value(MDR[31:28]));  // open: dp
  Hex_Digit_Display hex_digit_display_3 (.value(IR[31:28]));  // open: dp
  Hex_Digit_Display hex_digit_display_4 (.value(Command[31:28]));  // open: dp
  Hex_Digit_Display hex_digit_display_5 (.value(deb_r7[31:28]));  // open: dp
  Hex_Digit_Display hex_digit_display_6 (.value(deb_r6[31:28]));  // open: dp
  Hex_Digit_Display hex_digit_display_7 (.value(deb_r5[31:28]));  // open: dp
  Hex_Digit_Display hex_digit_display_8 (.value(deb_r4[31:28]));  // open: dp
  assign controlled_buffer_1_out = comparator_1_lt ? bitselector_1_out : 20'bz;  // Controlled_Buffer controlled_buffer_1
  Hex_Digit_Display hex_digit_display_9 (.value(PC[27:24]));  // open: dp
  Hex_Digit_Display hex_digit_display_10 (.value(PC[23:20]));  // open: dp
  Hex_Digit_Display hex_digit_display_11 (.value(MDR[27:24]));  // open: dp
  Hex_Digit_Display hex_digit_display_12 (.value(MDR[23:20]));  // open: dp
  Hex_Digit_Display hex_digit_display_13 (.value(IR[27:24]));  // open: dp
  Hex_Digit_Display hex_digit_display_14 (.value(IR[23:20]));  // open: dp
  Hex_Digit_Display hex_digit_display_15 (.value(Command[27:24]));  // open: dp
  Hex_Digit_Display hex_digit_display_16 (.value(Command[23:20]));  // open: dp
  Hex_Digit_Display hex_digit_display_17 (.value(deb_r7[27:24]));  // open: dp
  Hex_Digit_Display hex_digit_display_18 (.value(deb_r7[23:20]));  // open: dp
  Hex_Digit_Display hex_digit_display_19 (.value(deb_r6[27:24]));  // open: dp
  Hex_Digit_Display hex_digit_display_20 (.value(deb_r6[23:20]));  // open: dp
  Hex_Digit_Display hex_digit_display_21 (.value(deb_r5[27:24]));  // open: dp
  Hex_Digit_Display hex_digit_display_22 (.value(deb_r5[23:20]));  // open: dp
  Hex_Digit_Display hex_digit_display_23 (.value(deb_r4[27:24]));  // open: dp
  Hex_Digit_Display hex_digit_display_24 (.value(deb_r4[23:20]));  // open: dp
  and and_1 (and_1_out, comparator_1_lt, CPU_write);
  Hex_Digit_Display hex_digit_display_25 (.value(PC[19:16]));  // open: dp
  Hex_Digit_Display hex_digit_display_26 (.value(PC[15:12]));  // open: dp
  Hex_Digit_Display hex_digit_display_27 (.value(MDR[19:16]));  // open: dp
  Hex_Digit_Display hex_digit_display_28 (.value(MDR[15:12]));  // open: dp
  Hex_Digit_Display hex_digit_display_29 (.value(IR[19:16]));  // open: dp
  Hex_Digit_Display hex_digit_display_30 (.value(IR[15:12]));  // open: dp
  Hex_Digit_Display hex_digit_display_31 (.value(Command[19:16]));  // open: dp
  Hex_Digit_Display hex_digit_display_32 (.value(Command[15:12]));  // open: dp
  Hex_Digit_Display hex_digit_display_33 (.value(deb_r7[19:16]));  // open: dp
  Hex_Digit_Display hex_digit_display_34 (.value(deb_r7[15:12]));  // open: dp
  Hex_Digit_Display hex_digit_display_35 (.value(deb_r6[19:16]));  // open: dp
  Hex_Digit_Display hex_digit_display_36 (.value(deb_r6[15:12]));  // open: dp
  Hex_Digit_Display hex_digit_display_37 (.value(deb_r5[19:16]));  // open: dp
  Hex_Digit_Display hex_digit_display_38 (.value(deb_r5[15:12]));  // open: dp
  Hex_Digit_Display hex_digit_display_39 (.value(deb_r4[19:16]));  // open: dp
  Hex_Digit_Display hex_digit_display_40 (.value(deb_r4[15:12]));  // open: dp
  RAM #(.addrWidth(20), .dataWidth(32), .trigger("falling"), .\type ("nonvolatile")) ram_1 (
    .addr(controlled_buffer_1_out), .we(CPU_write), .oe(cpu_1_read), .clk(CLK),
    .din(controlled_buffer_2_out), .dout(ram_1_dout));
  assign controlled_buffer_2_out = and_1_out ? cpu_1_outdata : 32'bz;  // Controlled_Buffer controlled_buffer_2
  BitSelector #(.group(20), .width(32)) bitselector_2 (.in(in_1), .out(out_9), .sel(1'b0));
  Hex_Digit_Display hex_digit_display_41 (.value(PC[11:8]));  // open: dp
  Hex_Digit_Display hex_digit_display_42 (.value(PC[7:4]));  // open: dp
  Hex_Digit_Display hex_digit_display_43 (.value(MDR[11:8]));  // open: dp
  Hex_Digit_Display hex_digit_display_44 (.value(MDR[7:4]));  // open: dp
  Hex_Digit_Display hex_digit_display_45 (.value(IR[11:8]));  // open: dp
  Hex_Digit_Display hex_digit_display_46 (.value(IR[7:4]));  // open: dp
  Hex_Digit_Display hex_digit_display_47 (.value(Command[11:8]));  // open: dp
  Hex_Digit_Display hex_digit_display_48 (.value(Command[7:4]));  // open: dp
  Hex_Digit_Display hex_digit_display_49 (.value(deb_r7[11:8]));  // open: dp
  Hex_Digit_Display hex_digit_display_50 (.value(deb_r7[7:4]));  // open: dp
  Hex_Digit_Display hex_digit_display_51 (.value(deb_r6[11:8]));  // open: dp
  Hex_Digit_Display hex_digit_display_52 (.value(deb_r6[7:4]));  // open: dp
  Hex_Digit_Display hex_digit_display_53 (.value(deb_r5[11:8]));  // open: dp
  Hex_Digit_Display hex_digit_display_54 (.value(deb_r5[7:4]));  // open: dp
  Hex_Digit_Display hex_digit_display_55 (.value(deb_r4[11:8]));  // open: dp
  Hex_Digit_Display hex_digit_display_56 (.value(deb_r4[7:4]));  // open: dp
  Hex_Digit_Display hex_digit_display_57 (.value(PC[3:0]));  // open: dp
  Hex_Digit_Display hex_digit_display_58 (.value(MDR[3:0]));  // open: dp
  Hex_Digit_Display hex_digit_display_59 (.value(IR[3:0]));  // open: dp
  Hex_Digit_Display hex_digit_display_60 (.value(Command[3:0]));  // open: dp
  Hex_Digit_Display hex_digit_display_61 (.value(deb_r7[3:0]));  // open: dp
  Hex_Digit_Display hex_digit_display_62 (.value(deb_r6[3:0]));  // open: dp
  Hex_Digit_Display hex_digit_display_63 (.value(deb_r5[3:0]));  // open: dp
  Hex_Digit_Display hex_digit_display_64 (.value(deb_r4[3:0]));  // open: dp
  Hex_Digit_Display hex_digit_display_65 (.value(MAR[31:28]));  // open: dp
  Hex_Digit_Display hex_digit_display_66 (.value(deb_r3[31:28]));  // open: dp
  Hex_Digit_Display hex_digit_display_67 (.value(deb_r2[31:28]));  // open: dp
  Hex_Digit_Display hex_digit_display_68 (.value(deb_r1[31:28]));  // open: dp
  Hex_Digit_Display hex_digit_display_69 (.value(deb_r0[31:28]));  // open: dp
  and and_2 (and_2_out, comparator_1_lt, cpu_1_read);
  Hex_Digit_Display hex_digit_display_70 (.value(MAR[27:24]));  // open: dp
  Hex_Digit_Display hex_digit_display_71 (.value(MAR[23:20]));  // open: dp
  Hex_Digit_Display hex_digit_display_72 (.value({1'b0, Posta_A}));  // open: dp
  Hex_Digit_Display hex_digit_display_73 (.value(deb_r3[27:24]));  // open: dp
  Hex_Digit_Display hex_digit_display_74 (.value(deb_r3[23:20]));  // open: dp
  Hex_Digit_Display hex_digit_display_75 (.value(deb_r2[27:24]));  // open: dp
  Hex_Digit_Display hex_digit_display_76 (.value(deb_r2[23:20]));  // open: dp
  Hex_Digit_Display hex_digit_display_77 (.value(deb_r1[27:24]));  // open: dp
  Hex_Digit_Display hex_digit_display_78 (.value(deb_r1[23:20]));  // open: dp
  Hex_Digit_Display hex_digit_display_79 (.value(deb_r0[27:24]));  // open: dp
  Hex_Digit_Display hex_digit_display_80 (.value(deb_r0[23:20]));  // open: dp
  assign out_8 = and_2_out ? ram_1_dout : 32'bz;  // Controlled_Buffer controlled_buffer_3
  Hex_Digit_Display hex_digit_display_81 (.value(MAR[19:16]));  // open: dp
  Hex_Digit_Display hex_digit_display_82 (.value(MAR[15:12]));  // open: dp
  Hex_Digit_Display hex_digit_display_83 (.value(deb_r3[19:16]));  // open: dp
  Hex_Digit_Display hex_digit_display_84 (.value(deb_r3[15:12]));  // open: dp
  Hex_Digit_Display hex_digit_display_85 (.value(deb_r2[19:16]));  // open: dp
  Hex_Digit_Display hex_digit_display_86 (.value(deb_r2[15:12]));  // open: dp
  Hex_Digit_Display hex_digit_display_87 (.value(deb_r1[19:16]));  // open: dp
  Hex_Digit_Display hex_digit_display_88 (.value(deb_r1[15:12]));  // open: dp
  Hex_Digit_Display hex_digit_display_89 (.value(deb_r0[19:16]));  // open: dp
  Hex_Digit_Display hex_digit_display_90 (.value(deb_r0[15:12]));  // open: dp
  Hex_Digit_Display hex_digit_display_91 (.value(MAR[11:8]));  // open: dp
  Hex_Digit_Display hex_digit_display_92 (.value(MAR[7:4]));  // open: dp
  Hex_Digit_Display hex_digit_display_93 (.value({1'b0, Posta_B}));  // open: dp
  Hex_Digit_Display hex_digit_display_94 (.value(deb_r3[11:8]));  // open: dp
  Hex_Digit_Display hex_digit_display_95 (.value(deb_r3[7:4]));  // open: dp
  Hex_Digit_Display hex_digit_display_96 (.value(deb_r2[11:8]));  // open: dp
  Hex_Digit_Display hex_digit_display_97 (.value(deb_r2[7:4]));  // open: dp
  Hex_Digit_Display hex_digit_display_98 (.value(deb_r1[11:8]));  // open: dp
  Hex_Digit_Display hex_digit_display_99 (.value(deb_r1[7:4]));  // open: dp
  Hex_Digit_Display hex_digit_display_100 (.value(deb_r0[11:8]));  // open: dp
  Hex_Digit_Display hex_digit_display_101 (.value(deb_r0[7:4]));  // open: dp
  Hex_Digit_Display hex_digit_display_102 (.value(MAR[3:0]));  // open: dp
  Hex_Digit_Display hex_digit_display_103 (.value(deb_r3[3:0]));  // open: dp
  Hex_Digit_Display hex_digit_display_104 (.value(deb_r2[3:0]));  // open: dp
  Hex_Digit_Display hex_digit_display_105 (.value(deb_r1[3:0]));  // open: dp
  Hex_Digit_Display hex_digit_display_106 (.value(deb_r0[3:0]));  // open: dp
  Hex_Digit_Display hex_digit_display_107 (.value(deb_adr[31:28]));  // open: dp
  BitSelector #(.group(7), .width(32)) bitselector_3 (.in(cpu_1_outdata), .out(bitselector_3_out), .sel(3'b000));
  assign controlled_buffer_4_out = comparator_8_eq ? bitselector_3_out : 7'bz;  // Controlled_Buffer controlled_buffer_4
  Hex_Digit_Display hex_digit_display_108 (.value(deb_adr[27:24]));  // open: dp
  Hex_Digit_Display hex_digit_display_109 (.value(deb_adr[23:20]));  // open: dp
  Hex_Digit_Display hex_digit_display_110 (.value(deb_adr[19:16]));  // open: dp
  Hex_Digit_Display hex_digit_display_111 (.value(deb_adr[15:12]));  // open: dp
  BitSelector #(.group(21), .width(32)) bitselector_4 (.in(cpu_1_outdata), .out(bitselector_4_out), .sel(1'b0));
  and and_3 (and_3_out, comparator_7_eq, CPU_write);
  Register #(.width(1)) register_1 (.D(comparator_6_eq), .en(CPU_write), .clk(CLK), .Q(register_1_q));  // open: clr
  TTY #(.cols(64), .rows(32)) tty_1 (.data(controlled_buffer_4_out), .clk(CLK), .we(and_4_out));  // open: clr
  and and_4 (and_4_out, CPU_write, comparator_8_eq);
  Hex_Digit_Display hex_digit_display_112 (.value(deb_adr[11:8]));  // open: dp
  Hex_Digit_Display hex_digit_display_113 (.value(deb_adr[7:4]));  // open: dp
  LED led_1 (.in(Flag_Reg[0]));
  LED led_2 (.in(Flag_Reg[1]));
  LED led_3 (.in(Flag_Reg[2]));
  or or_1 (or_1_out, and_3_out, register_1_q);
  Hex_Digit_Display hex_digit_display_114 (.value(deb_adr[3:0]));  // open: dp
  Comparator comparator_9 (.a(IR[31:24]), .b(8'h1b), .eq(comparator_9_eq));  // open: gt, lt
  Comparator comparator_10 (.a(IR[31:24]), .b(8'h10), .eq(comparator_10_eq));  // open: gt, lt
  Comparator comparator_11 (.a(IR[31:24]), .b(8'h2), .eq(comparator_11_eq));  // open: gt, lt
  Comparator comparator_12 (.a(IR[31:24]), .b(8'h1), .eq(comparator_12_eq));  // open: gt, lt
  LED JMP (.in(comparator_9_eq));
  Register #(.width(21)) register_2 (.D(bitselector_4_out), .en(CPU_write), .clk(CLK), .Q(register_2_q));  // open: clr
  or or_2 (or_2_out, adr_posy, adr_posx, adr_color, adr_kmt);
  LED ADD (.in(comparator_10_eq));
  LED sGPU (.in(or_2_out));
  LED STR (.in(comparator_11_eq));
  // Buzzer buzzer_1: pin names not known; wires that end beside it: bitselector_4_out[13:0], bitselector_4_out[20:14], or_1_out, register_2_q[13:0], or_1_out, register_2_q[20:14], CPU_write, comparator_5_eq
  POR #(.PorHighDuration(1)) por_1 (.out(por_1_out));
  LED LOAD (.in(comparator_12_eq));
  Clock clock_1 (.out(CLK));
  // RGB_Video #(.cursor("No Cursor"), .height(32), .scale(8), .width(32)) rgb_video_1: pin names not known; wires that end beside it: por_1_out, CLK, 1'b1, rgb_video_1_p4, rgb_video_1_p5, rgb_video_1_p6
  and and_5 (and_5_out, CPU_write, adr_kmt);
  and and_6 (and_6_out, CPU_write, adr_color);
  and and_7 (and_7_out, CPU_write, adr_posx);
  and and_8 (and_8_out, CPU_write, adr_posy);
  Register #(.width(32)) register_3 (.D(cpu_1_outdata), .en(and_8_out), .clk(CLK));  // open: Q, clr
  GPU gpu_1 (
    .CLK(CLK), .kmt_we(and_5_out), .color_we(and_6_out), .posx_we(and_7_out), .posy_we(and_8_out),
    .Data(cpu_1_outdata), .out_color(rgb_video_1_p6), .deb_posx(rgb_video_1_p4), .deb_posy(rgb_video_1_p5));  // open: deb_kmt
  assign {bit_extender_1_out[7:5], bit_extender_1_out_2[0], bit_extender_1_out[3:0]} = {{3{rgb_video_1_p4[4]}}, rgb_video_1_p4};  // Bit_Extender bit_extender_1
  Hex_Digit_Display hex_digit_display_115 (.value({3'b000, bit_extender_1_out_2[0]}));  // open: dp
  Hex_Digit_Display hex_digit_display_116 (.value(bit_extender_1_out[3:0]));  // open: dp
  assign {bit_extender_2_out_3, bit_extender_2_out_2[0], bit_extender_2_out} = {{3{rgb_video_1_p5[4]}}, rgb_video_1_p5};  // Bit_Extender bit_extender_2
  Hex_Digit_Display hex_digit_display_117 (.value(rgb_video_1_p6));  // open: dp
  Hex_Digit_Display hex_digit_display_118 (.value({3'b000, bit_extender_2_out_2[0]}));  // open: dp
  Hex_Digit_Display hex_digit_display_119 (.value(bit_extender_2_out));  // open: dp
  // RGB_Video #(.cursor("No Cursor"), .height(32), .scale(8), .width(32)) rgb_video_2: pin names not known; wires that end beside it: in_2, in_3, in_4, in_5, in_6, in_7

  // Notes on the sheet:
  //   21: Read; MDR_we
  //   C0: MDR_out; IR_we
  //   8008:  pc_enb, mar_we | pc++; mar = pc;
  //   tty
  //   read
  //   write
  //   A < B
  //   A == B
  //   A > B
endmodule

module CPU (
  input  CLK,
  input  [31:0] inData,
  input  in_3,
  input  in_4,
  input  in_5,
  input  in_6,
  input  in_7,
  input  in_8,
  input  in_9,
  input  in_10,
  input  in_11,
  input  in_12,
  output [31:0] outAddress,
  output [31:0] outData,
  output Read,
  output Write,
  output [31:0] deb_PC,
  output [31:0] deb_MAR,
  output [31:0] deb_IR,
  output debSP,
  output [31:0] deb_MDR,
  output [2:0] debFlagReg,
  output [2:0] deb_posta_A,
  output [2:0] deb_posta_B,
  output [31:0] deb_r7,
  output [31:0] deb_r6,
  output [31:0] deb_r5,
  output [31:0] deb_r4,
  output [31:0] deb_r3,
  output [31:0] deb_r2,
  output [31:0] deb_r1,
  output [31:0] deb_r0,
  output [31:0] deb_AdrReg,
  output [31:0] out_34
);

  wire and_1_out, and_2_out, and_3_out, and_4_out, and_5_out, INT_we, Interrupt_q, or_1_out, undriven,
       undriven_2, undriven_3, undriven_4;
  wire [2:0] alu_1_cmp_less, Posta;
  wire [3:0] controlled_buffer_10_out;
  wire [7:0] adder_2_out, controlled_buffer_1_out, controlled_buffer_2_out, controlled_buffer_5_out,
       demultiplexer_1_out0, demultiplexer_1_out1, multiplexer_2_out, StackReg_q, StackRegister_q,
       subtractor_1_out;
  wire [31:0] ACC_q, adder_1_out, alu_1_alu_out, controlled_buffer_4_out, controlled_buffer_11_out,
       multiplexer_1_out, multiplexer_3_out, multiplexer_4_out, registerfile_1_regout, TEMP_q;

  Register #(.width(32)) MDR (.D(inData), .en(out_34[5]), .clk(CLK), .Q(deb_MDR));  // open: clr
  Register #(.width(32)) AddressRegister (
    .D(multiplexer_1_out), .en(out_34[16]), .clk(CLK), .Q(deb_AdrReg));  // open: clr
  Multiplexer #(.width(32)) multiplexer_1 (.in0(inData), .in1(adder_1_out), .out(multiplexer_1_out), .sel(out_34[18]));
  Register #(.width(1)) Interrupt (.D(undriven), .en(INT_we), .clk(CLK), .Q(Interrupt_q));  // open: clr
  assign controlled_buffer_1_out = in_3 ? controlled_buffer_2_out : 8'bz;  // Controlled_Buffer controlled_buffer_1
  Demultiplexer #(.width(8)) demultiplexer_1 (
    .out0(demultiplexer_1_out0), .out1(demultiplexer_1_out1), .in(controlled_buffer_2_out), .sel(in_4));
  assign controlled_buffer_2_out = in_5 ? StackRegister_q : 8'bz;  // Controlled_Buffer controlled_buffer_2
  assign outData = out_34[6] ? deb_MDR : 32'bz;  // Controlled_Buffer controlled_buffer_3
  assign controlled_buffer_4_out = out_34[17] ? deb_AdrReg : 32'bz;  // Controlled_Buffer controlled_buffer_4
  Adder #(.width(32)) adder_1 (.a(deb_AdrReg), .b(outData), .out(adder_1_out));  // open: cin, cout
  assign controlled_buffer_5_out = in_8 ? StackReg_q : 8'bz;  // Controlled_Buffer controlled_buffer_5
  RegisterFile registerfile_1 (
    .CLK(CLK), .inData(outData), .WE(out_34[26]), .REG_inSel(Posta), .REG_outSel(Posta),
    .OUT_enb(out_34[25]), .deb_reg0(deb_r0), .deb_reg1(deb_r1), .deb_reg2(deb_r2), .deb_reg3(deb_r3),
    .deb_reg4(deb_r4), .deb_reg5(deb_r5), .deb_reg6(deb_r6), .deb_reg7(deb_r7), .regOut(registerfile_1_regout));
  assign controlled_buffer_4_out = out_34[29] ? outData : 32'bz;  // Controlled_Buffer controlled_buffer_6
  Adder adder_2 (.a(demultiplexer_1_out0), .b(8'h1), .out(adder_2_out));  // open: cin, cout
  Subtractor subtractor_1 (.a(demultiplexer_1_out1), .b(8'h1), .out(subtractor_1_out));  // open: bin, bout
  assign registerfile_1_regout = out_34[28] ? outData : 32'bz;  // Controlled_Buffer controlled_buffer_7
  assign outData = out_34[27] ? registerfile_1_regout : 32'bz;  // Controlled_Buffer controlled_buffer_8
  Multiplexer #(.width(8)) multiplexer_2 (
    .in0(adder_2_out), .in1(subtractor_1_out), .out(multiplexer_2_out), .sel(in_4));
  and and_1 (and_1_out, undriven_2, or_1_out);
  or or_1 (or_1_out, undriven_3, undriven_4);
  Register #(.width(32)) TEMP (.D(registerfile_1_regout), .en(out_34[9]), .clk(CLK), .Q(TEMP_q));  // open: clr
  assign outData = out_34[30] ? TEMP_q : 32'bz;  // Controlled_Buffer controlled_buffer_9
  Register StackRegister (.D(multiplexer_2_out), .en(in_6), .clk(in_7), .Q(StackRegister_q));  // open: clr
  Counter StackReg (.load(in_10), .count(in_11), .Q(StackReg_q), .up(in_9), .clk(in_12));  // open: D, carry, clr
  Register #(.width(32)) InstructionRegister (.D(outData), .en(out_34[7]), .clk(CLK), .Q(deb_IR));  // open: clr
  Multiplexer #(.width(32)) multiplexer_3 (
    .in0(registerfile_1_regout), .in1(outData), .out(multiplexer_3_out), .sel(out_34[22]));
  assign controlled_buffer_10_out = out_34[19] ? deb_IR[27:24] : 4'bz;  // Controlled_Buffer controlled_buffer_10
  and and_2 (and_2_out, and_3_out, and_4_out);
  and and_3 (and_3_out, controlled_buffer_10_out[3], ~controlled_buffer_10_out[2]);  // AND_Gate
  and and_4 (and_4_out, ~controlled_buffer_10_out[1], ~controlled_buffer_10_out[0]);  // AND_Gate
  ALU alu_1 (
    .inA(TEMP_q), .inB(multiplexer_3_out), .I3B(controlled_buffer_10_out), .ALU_out(alu_1_alu_out),
    .cmp_greater(alu_1_cmp_less[2]), .cmp_equal(alu_1_cmp_less[1]), .cmp_less(alu_1_cmp_less[0]));
  assign controlled_buffer_11_out = out_34[4] ? controlled_buffer_4_out : 32'bz;  // Controlled_Buffer controlled_buffer_11
  ControlUnit controlunit_1 (
    .CLK(CLK), .IR_in(deb_IR), .flag_reg(debFlagReg), .controlBits(out_34), .posta(Posta),
    .deb_posta_A(deb_posta_A), .deb_posta_B(deb_posta_B));
  Register #(.width(32)) ACC (.D(alu_1_alu_out), .en(out_34[23]), .clk(CLK), .Q(ACC_q));  // open: clr
  Counter #(.max('hffffffff), .width(32)) ProgramCounter (
    .load(out_34[4]), .D(controlled_buffer_11_out), .count(out_34[3]), .Q(deb_PC), .clk(CLK));  // open: carry, up, clr
  Multiplexer #(.width(32)) multiplexer_4 (
    .in0(deb_PC), .in1(controlled_buffer_4_out), .out(multiplexer_4_out), .sel(out_34[2]));
  assign outData = out_34[21] ? ACC_q : 32'bz;  // Controlled_Buffer controlled_buffer_12
  Register #(.width(32)) MAR (.D(multiplexer_4_out), .en(out_34[15]), .clk(CLK), .Q(deb_MAR));  // open: clr
  and and_5 (and_5_out, and_2_out, out_34[19]);
  Register #(.width(3)) FlagRegister (.D(alu_1_cmp_less), .en(and_5_out), .clk(CLK), .Q(debFlagReg));  // open: clr

  assign outAddress = deb_MAR;
  assign Read = out_34[0];
  assign Write = out_34[1];

  // Other names for the same wires on the sheet: deb_ADR[31:0] = deb_AdrReg; deb_FlagReg[2:0] = debFlagReg;
  //   deb_postaA_Data[2:0] = deb_posta_A; deb_postaB_Data[2:0] = deb_posta_B; IR_data[31:0] = deb_IR;
  //   MDR_data[31:0] = deb_MDR; PC_mux = out_34[2]; PC_enb = out_34[3]; PC_load = out_34[4]; MDR_we = out_34[5];
  //   MDR_out = out_34[6]; IR_we = out_34[7]; IR_out = out_34[8]; TEMP_we = out_34[9]; Posta_A_we = out_34[10];
  //   Posta_A_out = out_34[11]; Posta_B_we = out_34[12]; Posta_B_out = out_34[13]; MAR_load = out_34[14];
  //   MAR_we = out_34[15]; ADR_we = out_34[16]; ADR_out = out_34[17]; ADR_mux = out_34[18]; I3B = out_34[19];
  //   ALU_in = out_34[20]; ALU_out = out_34[21]; ALU_mux = out_34[22]; ACC_we = out_34[23]; FR_cls = out_34[24];
  //   REG_out = out_34[25]; REG_we = out_34[26]; REG_data_out = out_34[27]; REG_path_in = out_34[28];
  //   DATA_to_adr = out_34[29]; TEMP_out = out_34[30]

  // Notes on the sheet:
  //   I3B
  //   carry
  //   Flagreg
  //   flagReg.m_carry
endmodule

module ALU (
  input  [31:0] inA,
  input  [31:0] inB,
  input  [3:0] I3B,
  output [31:0] ALU_out,
  output cmp_greater,
  output cmp_equal,
  output cmp_less
);

  wire adder_1_cout, subtractor_1_bout, undriven, undriven_2;
  wire [4:0] bit_extender_1_out;
  wire [31:0] adder_1_out, and_1_out, divider_1_out, multiplier_1_out, not_1_out, or_1_out, shifter_1_out,
       shifter_2_out, subtractor_1_out, xor_1_out;

  Bit_Extender #(.in_width(32), .out_width(5)) bit_extender_1 (.in(inB), .out(bit_extender_1_out));
  Adder #(.width(32)) adder_1 (.a(inA), .b(inB), .out(adder_1_out), .cin(undriven), .cout(adder_1_cout));
  Subtractor #(.width(32)) subtractor_1 (
    .a(inA), .b(inB), .out(subtractor_1_out), .bin(undriven_2), .bout(subtractor_1_bout));
  Multiplier #(.width(32)) multiplier_1 (.a(inA), .b(inB), .out(multiplier_1_out));  // open: cin, cout
  Divider #(.width(32)) divider_1 (.a(inA), .b(inB), .out(divider_1_out));  // open: upper, rem
  Comparator #(.width(32)) comparator_1 (.a(inA), .b(inB), .gt(cmp_greater), .eq(cmp_equal), .lt(cmp_less));
  Shifter #(.width(32)) shifter_1 (.in(inA), .\dist (bit_extender_1_out), .out(shifter_1_out));
  Shifter #(.shift("lr"), .width(32)) shifter_2 (.in(inA), .\dist (bit_extender_1_out), .out(shifter_2_out));
  assign and_1_out = inA & inB;  // AND_Gate and_1, 32 bits wide
  assign or_1_out = inA | inB;  // OR_Gate or_1, 32 bits wide
  assign xor_1_out = inA ^ inB;  // XOR_Gate xor_1, 32 bits wide
  assign not_1_out = ~inA;  // NOT_Gate not_1, 32 bits wide
  Multiplexer #(.select(4), .width(32)) multiplexer_1 (
    .in0(adder_1_out), .in1(subtractor_1_out), .in2(multiplier_1_out), .in3(divider_1_out), .in4(and_1_out),
    .in5(or_1_out), .in6(xor_1_out), .in7(not_1_out), .in9(shifter_1_out), .in10(shifter_2_out),
    .out(ALU_out), .sel(I3B));  // open: in8, in11, in12, in13, in14, in15
endmodule

module RegisterFile (
  input  CLK,
  input  [31:0] inData,
  input  WE,
  input  [2:0] REG_inSel,
  input  [2:0] REG_outSel,
  input  OUT_enb,
  output [31:0] deb_reg0,
  output [31:0] deb_reg1,
  output [31:0] deb_reg2,
  output [31:0] deb_reg3,
  output [31:0] deb_reg4,
  output [31:0] deb_reg5,
  output [31:0] deb_reg6,
  output [31:0] deb_reg7,
  output [31:0] regOut
);

  wire demultiplexer_1_out0, demultiplexer_1_out1, demultiplexer_1_out2, demultiplexer_1_out3,
       demultiplexer_1_out4, demultiplexer_1_out5, demultiplexer_1_out6, demultiplexer_1_out7;

  Demultiplexer #(.select(3)) demultiplexer_1 (
    .out0(demultiplexer_1_out0), .out1(demultiplexer_1_out1), .out2(demultiplexer_1_out2),
    .out3(demultiplexer_1_out3), .out4(demultiplexer_1_out4), .out5(demultiplexer_1_out5),
    .out6(demultiplexer_1_out6), .out7(demultiplexer_1_out7), .in(WE), .sel(REG_inSel));
  Register #(.width(32)) reg0 (.D(inData), .en(demultiplexer_1_out0), .clk(CLK), .Q(deb_reg0));  // open: clr
  Register #(.width(32)) reg1 (.D(inData), .en(demultiplexer_1_out1), .clk(CLK), .Q(deb_reg1));  // open: clr
  Register #(.width(32)) reg2 (.D(inData), .en(demultiplexer_1_out2), .clk(CLK), .Q(deb_reg2));  // open: clr
  Register #(.width(32)) reg3 (.D(inData), .en(demultiplexer_1_out3), .clk(CLK), .Q(deb_reg3));  // open: clr
  Register #(.width(32)) reg4 (.D(inData), .en(demultiplexer_1_out4), .clk(CLK), .Q(deb_reg4));  // open: clr
  Register #(.width(32)) reg5 (.D(inData), .en(demultiplexer_1_out5), .clk(CLK), .Q(deb_reg5));  // open: clr
  Register #(.width(32)) reg6 (.D(inData), .en(demultiplexer_1_out6), .clk(CLK), .Q(deb_reg6));  // open: clr
  Register #(.width(32)) reg7 (.D(inData), .en(demultiplexer_1_out7), .clk(CLK), .Q(deb_reg7));  // open: clr
  Multiplexer #(.enable("true"), .select(3), .width(32)) multiplexer_1 (
    .in0(deb_reg0), .in1(deb_reg1), .in2(deb_reg2), .in3(deb_reg3), .in4(deb_reg4), .in5(deb_reg5),
    .in6(deb_reg6), .in7(deb_reg7), .out(regOut), .sel(REG_outSel), .en(OUT_enb));
endmodule

module ControlUnit (
  input  CLK,
  input  [31:0] IR_in,
  input  [2:0] flag_reg,
  output [31:0] controlBits,
  output [2:0] posta,
  output [2:0] deb_posta_A,
  output [2:0] deb_posta_B
);

  wire and_1_out, and_2_out, and_3_out, and_4_out, and_5_out, and_6_out, decoder_1_out3, jmpdecoder_1_op_je,
       jmpdecoder_1_op_jgt, jmpdecoder_1_op_jlt, jmpdecoder_1_op_jne, or_1_out, or_2_out;
  wire [3:0] counter_1_q;
  wire [7:0] counter_2_q, rom_1_data;

  ROM #(.addrWidth(11)) rom_1 (.addr({IR_in[31:24], IR_in[17:15]}), .data(rom_1_data));
  Register #(.width(3)) postaA (.D(IR_in[23:21]), .en(controlBits[10]), .clk(CLK), .Q(deb_posta_A));  // open: clr
  Register #(.width(3)) postaB (.D(IR_in[20:18]), .en(controlBits[12]), .clk(CLK), .Q(deb_posta_B));  // open: clr
  Counter #(.max('hf), .width(4)) counter_1 (
    .Q(counter_1_q), .clk(CLK), .clr(or_1_out));  // open: load, D, count, carry, up
  Decoder #(.enable("false"), .select(4)) decoder_1 (
    .out3(decoder_1_out3), .sel(counter_1_q));  // open: out0, out1, out2, out4, out5, out6, out7, out8, out9, out10, out11, out12, out13, out14, out15
  Counter counter_2 (
    .load(decoder_1_out3), .D(rom_1_data), .Q(counter_2_q), .clk(CLK), .clr(or_1_out));  // open: count, carry, up
  assign posta = controlBits[11] ? deb_posta_A : 3'bz;  // Controlled_Buffer controlled_buffer_1
  assign posta = controlBits[13] ? deb_posta_B : 3'bz;  // Controlled_Buffer controlled_buffer_2
  ROM #(.dataWidth(32)) rom_2 (.addr(counter_2_q), .data(controlBits));
  or or_1 (or_1_out, and_2_out, and_1_out);
  and and_1 (and_1_out, controlBits[4], controlBits[3], controlBits[2], controlBits[1], controlBits[0]);
  JmpDecoder jmpdecoder_1 (
    .opcode(IR_in[31:24]), .op_JNE(jmpdecoder_1_op_jne), .op_JE(jmpdecoder_1_op_je),
    .op_JGT(jmpdecoder_1_op_jgt), .op_JLT(jmpdecoder_1_op_jlt));
  and and_2 (and_2_out, decoder_1_out3, or_2_out);
  and and_3 (and_3_out, flag_reg[1], jmpdecoder_1_op_jne);
  or or_2 (or_2_out, and_3_out, and_4_out, and_5_out, and_6_out);
  and and_4 (and_4_out, ~flag_reg[1], jmpdecoder_1_op_je);  // AND_Gate
  and and_5 (and_5_out, ~flag_reg[2], jmpdecoder_1_op_jgt);  // AND_Gate
  and and_6 (and_6_out, ~flag_reg[0], jmpdecoder_1_op_jlt);  // AND_Gate

  // Other names for the same wires on the sheet: POSTA_A_we = controlBits[10]; POSTA_A_out = controlBits[11];
  //   POSTA_B_we = controlBits[12]; POSTA_B_out = controlBits[13]

  // Notes on the sheet:
  //   contents of rom_1 (hex, n*v repeats v):
  //   9*0 5 9 f 6*0 14 45*0 19 64*0 1d 2d 34 0 28 0 0 0 1d 2d 34 0 28 0 0 0 1d 2d 34 0 28 0 0 0 1d 2d 34 0
  //   28 7*0 28 7*0 28 7*0 28 0 0 3a 8*0 23 0 0 0 36 7*0 28 7*0 28 0 0 3f 7*0 3f 7*0 3f 7*0 3f 7*0 3f
  //   contents of rom_2 (hex, n*v repeats v):
  //   8008 21 c0 0 1f 9008 21 4002040 1f 9008 10001 28004 21 4002040 1f 1400 2a00a004 21 4000840 1f 9008
  //   10001 28004 a002002 1f 1400 2002200 44000800 1f 9008 21 2002200 c80040 4202000 1f 9008 21 2002200
  //   480040 1f 1400 2000a00 2882000 4200800 1f 9008 10001 28004 2002221 c80040 4202000 1f 400 1f 1400
  //   2000a00 2082000 1f 1000 2002200 2882000 4202000 1f 8008 10001 20010 1f
  //   0: <
  //   1 : ==
  //   2 : >
  //   jne !=
  //   je ==
  //   jgt >
  //   jlt <
endmodule

module JmpDecoder (
  input  [7:0] opcode,
  output op_JNE,
  output op_JE,
  output op_JGT,
  output op_JLT
);

  Comparator comparator_1 (.a(opcode), .b(8'h1c), .eq(op_JNE));  // open: gt, lt
  Comparator comparator_2 (.a(opcode), .b(8'h1d), .eq(op_JE));  // open: gt, lt
  Comparator comparator_3 (.a(opcode), .b(8'h1e), .eq(op_JGT));  // open: gt, lt
  Comparator comparator_4 (.a(opcode), .b(8'h1f), .eq(op_JLT));  // open: gt, lt
endmodule

module GPU (
  input  CLK,
  input  kmt_we,
  input  color_we,
  input  posx_we,
  input  posy_we,
  input  [31:0] Data,
  output [1:0] deb_kmt,
  output [3:0] out_color,
  output [4:0] deb_posx,
  output [4:0] deb_posy
);

  wire and_1_out, and_2_out, decoder_1_out1, decoder_2_out5, decoder_2_out7, register_1_q;
  wire [3:0] counter_1_q;

  Register #(.width(2)) kmt (.D(Data[1:0]), .en(kmt_we), .clk(CLK), .Q(deb_kmt), .clr(and_1_out));
  Register #(.width(4)) color (.D(Data[3:0]), .en(color_we), .clk(CLK), .Q(out_color));  // open: clr
  Register #(.width(5)) posx_t (.D(Data[4:0]), .en(posx_we), .clk(CLK), .Q(deb_posx));  // open: clr
  Register #(.width(5)) posy_t (.D(Data[4:0]), .en(posy_we), .clk(CLK), .Q(deb_posy));  // open: clr
  Decoder #(.enable("false"), .select(2)) decoder_1 (.out1(decoder_1_out1), .sel(deb_kmt));  // open: out0, out2, out3
  Counter #(.max('hf), .width(4)) counter_1 (.Q(counter_1_q), .clk(CLK));  // open: load, D, count, carry, up, clr
  Decoder #(.enable("false"), .select(4)) decoder_2 (
    .out5(decoder_2_out5), .out7(decoder_2_out7), .sel(counter_1_q));  // open: out0, out1, out2, out3, out4, out6, out8, out9, out10, out11, out12, out13, out14, out15
  and and_1 (and_1_out, decoder_2_out7, register_1_q, decoder_1_out1);
  and and_2 (and_2_out, decoder_1_out1, decoder_2_out5);
  Register #(.width(1)) register_1 (.D(and_2_out), .en(and_2_out), .clk(CLK), .Q(register_1_q));  // open: clr

  // Notes on the sheet:
  //   px
  //   py
endmodule
