// Logisim project t1_keyboardInput.circ as structural Verilog: 1 circuit, main circuit main
module main (
  input  [31:0] in_1,
  input  in_2,
  input  in_3,
  input  in_4
);

  wire and_1_out, and_2_out, clock_1_out, counter_1_carry, counter_2_carry, decoder_1_out0, decoder_1_out1,
       keyboard_1_avail, register_1_q;
  wire [2:0] controlled_buffer_1_out, ram_1_dout;
  wire [3:0] controlled_buffer_1_out_2, counter_1_q, counter_3_q;
  wire [5:0] counter_2_q;
  wire [6:0] keyboard_1_data;
  wire [9:0] multiplexer_1_out;
  wire [12:0] rom_1_data;

  Counter #(.max('hf), .width(4)) counter_1 (
    .Q(counter_1_q), .carry(counter_1_carry), .clk(clock_1_out));  // open: load, D, count, up, clr
  Decoder #(.enable("false")) decoder_1 (.out0(decoder_1_out0), .out1(decoder_1_out1), .sel(in_2));
  ROM #(.addrWidth(4), .dataWidth(13)) rom_1 (.addr(counter_1_q), .data(rom_1_data));
  Clock clock_1 (.out(clock_1_out));
  and and_1 (and_1_out, clock_1_out, register_1_q);
  Keyboard keyboard_1 (.clk(and_1_out), .clr(in_1[0]), .avail(keyboard_1_avail), .data(keyboard_1_data));  // open: re
  assign {controlled_buffer_1_out_2, controlled_buffer_1_out} = decoder_1_out0 ? keyboard_1_data : 7'bz;  // Controlled_Buffer controlled_buffer_1
  Register #(.width(1)) register_1 (.D(keyboard_1_avail), .en(1'b1), .clk(clock_1_out), .Q(register_1_q));  // open: clr
  Hex_Digit_Display hex_digit_display_1 (.value(controlled_buffer_1_out_2));  // open: dp
  Hex_Digit_Display hex_digit_display_2 (.value({1'b0, controlled_buffer_1_out}));  // open: dp
  Multiplexer #(.width(10)) multiplexer_1 (
    .in0({counter_3_q, counter_2_q}), .in1(rom_1_data[9:0]), .out(multiplexer_1_out), .sel(and_2_out));
  and and_2 (and_2_out, in_3, ~counter_1_carry);  // AND_Gate
  RAM #(.addrWidth(10), .dataWidth(3)) ram_1 (
    .addr(multiplexer_1_out), .we(in_4), .oe(1'b1), .clk(clock_1_out), .din(rom_1_data[12:10]),
    .dout(ram_1_dout));
  Counter #(.max('h3f), .width(6)) counter_2 (
    .Q(counter_2_q), .carry(counter_2_carry), .clk(clock_1_out));  // open: load, D, count, up, clr
  Counter #(.max('hf), .width(4)) counter_3 (
    .count(counter_2_carry), .Q(counter_3_q), .clk(clock_1_out));  // open: load, D, carry, up, clr
  // RGB_Video #(.height(16), .scale(8), .width(64)) rgb_video_1: pin names not known; wires that end beside it: clock_1_out, 1'b1, counter_2_q, counter_3_q, ram_1_dout

  // Notes on the sheet:
  //   contents of rom_1 (hex, n*v repeats v):
  //   1000 1000 1000
endmodule
