// Logisim project t5_CharsetROM.circ as structural Verilog: 1 circuit, main circuit main
module main (
  input  in_1,
  input  in_2,
  input  in_3,
  input  in_4,
  input  in_5,
  input  in_6
);

  wire and_1_out, and_2_out, and_3_out, and_4_out, bitselector_1_out, CLK, comparator_1_eq, counter_3_carry,
       counter_4_carry, counter_5_carry, counter_7_carry, decoder_1_out1, decoder_1_out2, decoder_1_out3,
       decoder_1_out4, not_1_out, or_1_out, px_carry, sx_carry;
  wire [2:0] controlled_buffer_1_out, controlled_buffer_2_out, counter_1_q, counter_3_q, counter_4_q,
       ram_1_dout;
  wire [4:0] px_q, py_q;
  wire [5:0] counter_7_q, counter_8_q;
  wire [6:0] counter_5_q, rgb_video_2_p4;
  wire [7:0] bit_extender_1_out, bit_extender_2_out, bit_extender_3_out, bit_extender_4_out, counter_2_q,
       multiplier_1_out, multiplier_2_out, rom_1_data;
  wire [15:0] adder_1_out, multiplexer_1_out, sx_q;

  and and_1 (and_1_out, and_4_out, ~and_2_out);  // AND_Gate
  Counter #(.max('h7), .width(3)) counter_1 (
    .count(and_1_out), .Q(counter_1_q), .clk(CLK), .clr(in_3));  // open: load, D, carry, up
  and and_2 (and_2_out, decoder_1_out2, ~counter_4_carry);  // AND_Gate
  Decoder #(.select(3)) decoder_1 (
    .out1(decoder_1_out1), .out2(decoder_1_out2), .out3(decoder_1_out3), .out4(decoder_1_out4),
    .sel(counter_1_q));  // open: out0, out5, out6, out7, en
  and and_3 (and_3_out, counter_3_carry, ~comparator_1_eq);  // AND_Gate
  Comparator comparator_1 (.a(counter_2_q), .b(8'h6), .eq(comparator_1_eq));  // open: gt, lt
  Counter counter_2 (.count(and_3_out), .Q(counter_2_q), .clk(CLK), .clr(in_1));  // open: load, D, carry, up
  ROM rom_1 (.addr(counter_2_q), .data(rom_1_data));
  and and_4 (and_4_out, in_2, ~decoder_1_out4);  // AND_Gate
  or or_1 (or_1_out, decoder_1_out1, decoder_1_out2);
  Counter #(.max('h1f), .width(5)) px (
    .count(decoder_1_out3), .Q(px_q), .carry(px_carry), .clk(CLK), .clr(in_4));  // open: load, D, up
  Counter #(.max('h1f), .width(5)) py (.count(px_carry), .Q(py_q), .clk(CLK), .clr(in_6));  // open: load, D, carry, up
  assign bit_extender_1_out = {{3{1'b0}}, py_q};  // Bit_Extender bit_extender_1
  Clock clock_1 (.out(CLK));
  assign bit_extender_2_out = {{3{1'b0}}, px_q};  // Bit_Extender bit_extender_2
  Multiplier multiplier_1 (.a(8'h8), .b(bit_extender_1_out), .out(multiplier_1_out));  // open: cin, cout
  Multiplier multiplier_2 (.a(8'h8), .b(bit_extender_2_out), .out(multiplier_2_out));  // open: cin, cout
  Counter #(.max('h7), .width(3)) counter_3 (
    .count(or_1_out), .Q(counter_3_q), .carry(counter_3_carry), .clk(CLK), .clr(in_5));  // open: load, D, up
  Multiplexer #(.width(16)) multiplexer_1 (.in0(sx_q), .in1(adder_1_out), .out(multiplexer_1_out), .sel(and_4_out));
  BitSelector bitselector_1 (.in(rom_1_data), .out(bitselector_1_out), .sel(counter_3_q));
  assign bit_extender_3_out = {{5{1'b0}}, counter_3_q};  // Bit_Extender bit_extender_3
  Counter #(.max('h7), .width(3)) counter_4 (
    .count(counter_3_carry), .Q(counter_4_q), .carry(counter_4_carry), .clk(CLK), .clr(in_5));  // open: load, D, up
  RAM #(.addrWidth(16), .dataWidth(3)) ram_1 (
    .addr(multiplexer_1_out), .we(and_4_out), .oe(1'b1), .clk(CLK), .din(controlled_buffer_1_out),
    .dout(ram_1_dout));
  assign controlled_buffer_1_out = and_4_out ? controlled_buffer_2_out : 3'bz;  // Controlled_Buffer controlled_buffer_1
  not not_1 (not_1_out, bitselector_1_out);
  assign controlled_buffer_2_out = bitselector_1_out ? 3'b111 : 3'bz;  // Controlled_Buffer controlled_buffer_2
  Hex_Digit_Display hex_digit_display_1 (.value(adder_1_out[7:4]));  // open: dp
  Adder adder_1 (.a(multiplier_2_out), .b(bit_extender_3_out), .out(adder_1_out[7:0]));  // open: cin, cout
  Counter sx (.Q(sx_q[7:0]), .carry(sx_carry), .clk(CLK));  // open: load, D, count, up, clr
  Hex_Digit_Display hex_digit_display_2 (.value(adder_1_out[3:0]));  // open: dp
  assign bit_extender_4_out = {{5{1'b0}}, counter_4_q};  // Bit_Extender bit_extender_4
  // RGB_Video #(.cursor("No Cursor"), .height(256), .width(256)) rgb_video_1: pin names not known; wires that end beside it: CLK, 1'b1, sx_q[7:0], sx_q[15:8], ram_1_dout
  Counter sy (.count(sx_carry), .Q(sx_q[15:8]), .clk(CLK));  // open: load, D, carry, up, clr
  assign controlled_buffer_2_out = not_1_out ? 3'b000 : 3'bz;  // Controlled_Buffer controlled_buffer_3
  Adder adder_2 (.a(bit_extender_4_out), .b(multiplier_1_out), .out(adder_1_out[15:8]));  // open: cin, cout
  Hex_Digit_Display hex_digit_display_3 (.value(adder_1_out[15:12]));  // open: dp
  Hex_Digit_Display hex_digit_display_4 (.value(adder_1_out[11:8]));  // open: dp
  Counter #(.max('h7f), .width(7)) counter_5 (
    .Q(counter_5_q), .carry(counter_5_carry), .clk(CLK));  // open: load, D, count, up, clr
  // RGB_Video #(.cursor("No Cursor"), .scale(4)) rgb_video_2: pin names not known; wires that end beside it: CLK, 1'b1, counter_5_q, rgb_video_2_p4, 7'b0000100
  Counter #(.max('h7f), .width(7)) counter_6 (
    .count(counter_5_carry), .Q(rgb_video_2_p4), .clk(CLK));  // open: load, D, carry, up, clr
  Counter #(.max('h3f), .width(6)) counter_7 (
    .Q(counter_7_q), .carry(counter_7_carry), .clk(CLK));  // open: load, D, count, up, clr
  Counter #(.max('h3f), .width(6)) counter_8 (
    .count(counter_7_carry), .Q(counter_8_q), .clk(CLK));  // open: load, D, carry, up, clr
  // RGB_Video #(.cursor("No Cursor"), .height(64), .scale(8), .width(64)) rgb_video_3: pin names not known; wires that end beside it: CLK, 1'b1, counter_7_q, counter_8_q, 7'b0000100

  // Notes on the sheet:
  //   contents of rom_1 (hex, n*v repeats v):
  //   7*ff
  //   ~30sn temizleme 2dk video => ~ 1 saat
endmodule
