// Logisim project t6_CharsetROM_128x128.circ as structural Verilog: 1 circuit, main circuit main
module main (
  input  in_1,
  input  in_2
);

  wire and_1_out, and_2_out, and_3_out, and_4_out, bitselector_1_out, CLK, comparator_1_eq, counter_4_carry,
       counter_6_carry, counter_7_carry, decoder_1_out0, decoder_1_out1, decoder_1_out2, decoder_1_out3,
       decoder_1_out4, not_1_out, not_2_out, or_1_out;
  wire [1:0] undriven_2, undriven_3;
  wire [2:0] controlled_buffer_1_out, controlled_buffer_2_out, counter_1_q, counter_6_q, counter_7_q,
       ram_1_dout;
  wire [6:0] bit_extender_1_out, bit_extender_2_out, bit_extender_3_out, bit_extender_4_out,
       multiplier_1_out, multiplier_2_out;
  wire [7:0] counter_2_q, counter_3_q, rom_1_data, undriven;
  wire [13:0] adder_1_out, counter_5_q, multiplexer_1_out;

  and and_1 (and_1_out, and_4_out, ~and_3_out);  // AND_Gate
  and and_2 (and_2_out, counter_6_carry, ~comparator_1_eq);  // AND_Gate
  Comparator comparator_1 (.a(counter_2_q), .b(8'h7), .eq(comparator_1_eq));  // open: gt, lt
  Counter #(.max('h7), .width(3)) counter_1 (
    .count(and_1_out), .Q(counter_1_q), .clk(CLK), .clr(in_2));  // open: load, D, carry, up
  and and_3 (and_3_out, decoder_1_out2, ~counter_7_carry);  // AND_Gate
  ROM rom_1 (
    .addr(counter_2_q),
    .data({rom_1_data[0], rom_1_data[1], rom_1_data[2], rom_1_data[3], rom_1_data[4], rom_1_data[5], rom_1_data[6], rom_1_data[7]}));
  Counter counter_2 (.count(and_2_out), .Q(counter_2_q), .clk(CLK), .clr(in_2));  // open: load, D, carry, up
  Decoder #(.select(3)) decoder_1 (
    .out0(decoder_1_out0), .out1(decoder_1_out1), .out2(decoder_1_out2), .out3(decoder_1_out3),
    .out4(decoder_1_out4), .sel(counter_1_q));  // open: out5, out6, out7, en
  Clock clock_1 (.out(CLK));
  and and_4 (and_4_out, in_1, ~decoder_1_out4);  // AND_Gate
  Counter counter_3 (.count(decoder_1_out3), .Q(counter_3_q), .clk(CLK));  // open: load, D, carry, up, clr
  or or_1 (or_1_out, decoder_1_out1, decoder_1_out2);
  not not_1 (not_1_out, and_4_out);
  Multiplexer #(.width(14)) multiplexer_1 (
    .in0(counter_5_q), .in1(adder_1_out), .out(multiplexer_1_out), .sel(and_4_out));
  // XOR_Gate xor_1 has open pins: in0={8{1'b1}}, in1=undriven, out=open
  assign bit_extender_1_out = {{3{1'b0}}, counter_3_q[3:0]};  // Bit_Extender bit_extender_1
  assign bit_extender_2_out = {{3{1'b0}}, counter_3_q[7:4]};  // Bit_Extender bit_extender_2
  Counter #(.max('h7f), .width(7)) counter_4 (
    .count(not_1_out), .Q(counter_5_q[6:0]), .carry(counter_4_carry), .clk(CLK));  // open: load, D, up, clr
  Counter #(.max('h7f), .width(7)) counter_5 (
    .count(counter_4_carry), .Q(counter_5_q[13:7]), .clk(CLK));  // open: load, D, carry, up, clr
  RAM #(.addrWidth(14), .dataWidth(3), .trigger("falling")) ram_1 (
    .addr(multiplexer_1_out), .we(and_4_out), .oe(1'b1), .clk(CLK), .din(controlled_buffer_1_out),
    .dout(ram_1_dout));
  Multiplier #(.width(7)) multiplier_1 (
    .a(7'b0001000), .b(bit_extender_1_out), .out(multiplier_1_out));  // open: cin, cout
  Counter #(.max('h7), .width(3)) counter_6 (
    .count(or_1_out), .Q(counter_6_q), .carry(counter_6_carry), .clk(CLK), .clr(decoder_1_out0));  // open: load, D, up
  Multiplier #(.width(7)) multiplier_2 (
    .a(7'b0001000), .b(bit_extender_2_out), .out(multiplier_2_out));  // open: cin, cout
  // RGB_Video #(.cursor("No Cursor"), .scale(4)) rgb_video_1: pin names not known; wires that end beside it: CLK, 1'b1, counter_5_q[6:0], counter_5_q[13:7], ram_1_dout
  BitSelector bitselector_1 (.in(rom_1_data), .out(bitselector_1_out), .sel(counter_6_q));
  assign bit_extender_3_out = {{4{1'b0}}, counter_6_q};  // Bit_Extender bit_extender_3
  Counter #(.max('h7), .width(3)) counter_7 (
    .count(counter_6_carry), .Q(counter_7_q), .carry(counter_7_carry), .clk(CLK), .clr(decoder_1_out0));  // open: load, D, up
  assign controlled_buffer_1_out = and_4_out ? controlled_buffer_2_out : 3'bz;  // Controlled_Buffer controlled_buffer_1
  not not_2 (not_2_out, bitselector_1_out);
  Adder #(.width(7)) adder_1 (.a(multiplier_1_out), .b(bit_extender_3_out), .out(adder_1_out[6:0]));  // open: cin, cout
  assign controlled_buffer_2_out = bitselector_1_out ? 3'b111 : 3'bz;  // Controlled_Buffer controlled_buffer_2
  Hex_Digit_Display hex_digit_display_1 (.value({undriven_2, adder_1_out[5:4]}));  // open: dp
  Hex_Digit_Display hex_digit_display_2 (.value(adder_1_out[3:0]));  // open: dp
  assign bit_extender_4_out = {{4{1'b0}}, counter_7_q};  // Bit_Extender bit_extender_4
  assign controlled_buffer_2_out = not_2_out ? 3'b000 : 3'bz;  // Controlled_Buffer controlled_buffer_3
  Adder #(.width(7)) adder_2 (
    .a(bit_extender_4_out), .b(multiplier_2_out), .out(adder_1_out[13:7]));  // open: cin, cout
  Hex_Digit_Display hex_digit_display_3 (.value({undriven_3, adder_1_out[12:11]}));  // open: dp
  Hex_Digit_Display hex_digit_display_4 (.value(adder_1_out[10:7]));  // open: dp

  // Notes on the sheet:
  //   contents of rom_1 (hex, n*v repeats v):
  //   7c 82 82 fe 82 82 82 0 fc 82 82 8c 82 82 fc
endmodule
