// Logisim project t7_lineAlgoTest.circ as structural Verilog: 2 circuits, main circuit main
module main (
  input  in_1,
  input  in_2,
  input  in_3,
  input  in_4,
  input  in_5,
  input  [7:0] in_6,
  input  [7:0] in_7,
  input  in_8,
  input  [7:0] in_9,
  input  [7:0] in_10,
  output [7:0] out_11
);

  wire and_1_out, and_2_out, ascii_t0_1_cx_clear, ascii_t0_1_muxt, CLK, comparator_1_eq, comparator_1_gt,
       comparator_1_lt, comparator_2_gt, controlled_buffer_2_out, counter_2_carry, decoder_1_out0,
       decoder_1_out1, decoder_1_out2, decoder_1_out3, decoder_1_out4, decoder_1_out5, decoder_1_out6,
       not_1_out, not_2_out, or_1_out, or_2_out, or_3_out, or_4_out, switch_1_p1;
  wire [2:0] ascii_t0_1_color, counter_1_q, ram_1_dout;
  wire [5:0] Color_q, command_q, undriven, undriven_3;
  wire [7:0] adder_1_out, adder_2_out, controlled_buffer_1_out, counter_4_q, data_q, data_q_2, data_q_3,
       data_q_4, divider_1_out, dx_q, dy_q, error_q, multiplexer_1_out, register_1_q, register_2_q,
       register_3_q, register_4_q, slope_dxdy_q, subtractor_1_out, subtractor_2_out, subtractor_3_out;
  wire [13:0] ascii_t0_1_posxy, multiplexer_2_out, rgb_video_1_p4;
  wire [31:0] undriven_2;

  not not_1 (not_1_out, controlled_buffer_2_out);
  Counter #(.max('h7), .width(3)) counter_1 (
    .count(not_1_out), .Q(counter_1_q), .clk(CLK));  // open: load, D, carry, up, clr
  Decoder #(.select(3)) decoder_1 (
    .out0(decoder_1_out0), .out1(decoder_1_out1), .out2(decoder_1_out2), .out3(decoder_1_out3),
    .out4(decoder_1_out4), .out5(decoder_1_out5), .out6(decoder_1_out6), .sel(counter_1_q));  // open: out7, en
  Clock clock_1 (.out(CLK));
  Multiplexer #(.width(8)) multiplexer_1 (.in0(8'ha), .in1(adder_1_out), .out(multiplexer_1_out), .sel(and_1_out));
  Register #(.width(6)) Color (.D(undriven), .en(in_3), .clk(CLK), .Q(Color_q));  // open: clr
  and and_1 (and_1_out, decoder_1_out6, comparator_2_gt);
  Register #(.width(32)) data (
    .D(undriven_2), .en(in_4), .clk(CLK), .Q({data_q_4, data_q_3, data_q_2, data_q}));  // open: clr
  Register #(.width(6)) command (.D(undriven_3), .en(in_5), .clk(CLK), .Q(command_q));  // open: clr
  Register register_1 (.D(8'h5), .en(decoder_1_out0), .clk(CLK), .Q(register_1_q));  // open: clr
  Register register_2 (.D(8'h14), .en(decoder_1_out0), .clk(CLK), .Q(register_2_q));  // open: clr
  Register register_3 (.D(multiplexer_1_out), .en(or_1_out), .clk(CLK), .Q(register_3_q));  // open: clr
  Register register_4 (.D(8'h28), .en(decoder_1_out0), .clk(CLK), .Q(register_4_q));  // open: clr
  or or_1 (or_1_out, decoder_1_out0, and_1_out);
  or or_2 (or_2_out, decoder_1_out6, decoder_1_out4);
  ASCII_t0 ascii_t0_1 (
    .charIn(data_q[6:0]), .CLK(CLK), .drawChar(in_1), .reset(in_2), .color_a(Color_q[2:0]),
    .color_b(Color_q[5:3]), .cx_clear(ascii_t0_1_cx_clear), .Color(ascii_t0_1_color), .muxt(ascii_t0_1_muxt),
    .posxy(ascii_t0_1_posxy));
  // Switch switch_1: pin names not known; wires that end beside it: switch_1_p1, ascii_t0_1_cx_clear
  Subtractor subtractor_1 (.a(register_1_q), .b(register_2_q), .out(subtractor_1_out));  // open: bin, bout
  Subtractor subtractor_2 (.a(register_3_q), .b(register_4_q), .out(subtractor_2_out));  // open: bin, bout
  Adder adder_1 (.a(register_3_q), .b(8'h1), .out(adder_1_out));  // open: cin, cout
  Register dx (.D(subtractor_1_out), .en(decoder_1_out1), .clk(CLK), .Q(dx_q));  // open: clr
  Register dy (.D(subtractor_2_out), .en(decoder_1_out1), .clk(CLK), .Q(dy_q));  // open: clr
  Multiplexer #(.width(14)) multiplexer_2 (
    .in0(rgb_video_1_p4), .in1(ascii_t0_1_posxy), .out(multiplexer_2_out), .sel(ascii_t0_1_muxt));
  Counter #(.max('h7f), .width(7)) counter_2 (
    .count(switch_1_p1), .Q(rgb_video_1_p4[6:0]), .carry(counter_2_carry), .clk(CLK));  // open: load, D, up, clr
  RAM #(.addrWidth(14), .dataWidth(3), .trigger("falling")) ram_1 (
    .addr(multiplexer_2_out), .we(ascii_t0_1_muxt), .oe(1'b1), .clk(CLK), .din(ascii_t0_1_color),
    .dout(ram_1_dout));
  // RGB_Video #(.cursor("No Cursor"), .scale(4)) rgb_video_1: pin names not known; wires that end beside it: CLK, 1'b1, rgb_video_1_p4[6:0], rgb_video_1_p4[13:7], ram_1_dout
  Counter #(.max('h7f), .width(7)) counter_3 (
    .count(counter_2_carry), .Q(rgb_video_1_p4[13:7]), .clk(CLK));  // open: load, D, carry, up, clr
  Divider #(.mode("twosComplement")) divider_1 (.a(dy_q), .b(dx_q), .out(divider_1_out), .rem(out_11));  // open: upper
  Counter counter_4 (
    .load(decoder_1_out5), .D(register_1_q), .count(or_2_out), .Q(counter_4_q), .clk(CLK));  // open: carry, up, clr
  Register slope_dxdy (.D(divider_1_out), .en(decoder_1_out2), .clk(CLK), .Q(slope_dxdy_q));  // open: clr
  or or_3 (or_3_out, decoder_1_out0, decoder_1_out6, decoder_1_out3);
  Register error (.D(adder_2_out), .en(or_3_out), .clk(CLK), .Q(error_q), .clr(decoder_1_out0));
  Comparator comparator_1 (
    .a(counter_4_q), .b(register_2_q), .gt(comparator_1_gt), .eq(comparator_1_eq), .lt(comparator_1_lt));
  assign controlled_buffer_1_out = in_8 ? error_q : 8'bz;  // Controlled_Buffer controlled_buffer_1
  Adder adder_2 (.a(slope_dxdy_q), .b(controlled_buffer_1_out), .out(adder_2_out));  // open: cin, cout
  Comparator #(.mode("unsigned")) comparator_2 (.a(error_q), .b(8'h1), .gt(comparator_2_gt));  // open: eq, lt
  Subtractor subtractor_3 (.a(error_q), .b(8'h1), .out(subtractor_3_out));  // open: bin, bout
  or or_4 (or_4_out, comparator_1_gt, comparator_1_eq);
  assign controlled_buffer_2_out = and_2_out ? comparator_1_lt : 1'bz;  // Controlled_Buffer controlled_buffer_2
  and and_2 (and_2_out, comparator_1_lt, decoder_1_out6);
  assign adder_2_out = comparator_2_gt ? subtractor_3_out : 8'bz;  // Controlled_Buffer controlled_buffer_3
  assign controlled_buffer_2_out = not_2_out ? or_4_out : 1'bz;  // Controlled_Buffer controlled_buffer_4
  not not_2 (not_2_out, and_2_out);

  // Notes on the sheet:
  //   a(5,10) b(20,40)
endmodule

module ASCII_t0 (
  input  [6:0] charIn,
  input  CLK,
  input  drawChar,
  input  reset,
  input  [2:0] color_a,
  input  [2:0] color_b,
  output cx_clear,
  output [2:0] Color,
  output muxt,
  output [13:0] posxy
);

  wire and_1_out, and_2_out, and_3_out, bitselector_1_out, comparator_1_eq, counter_4_carry, counter_5_carry,
       decoder_1_out0, decoder_1_out1, decoder_1_out2, decoder_1_out3, decoder_1_out4, not_2_out, or_1_out;
  wire [1:0] undriven_2, undriven_3;
  wire [2:0] controlled_buffer_2_out, counter_1_q, counter_4_q, counter_5_q;
  wire [6:0] bit_extender_1_out, bit_extender_2_out, bit_extender_3_out, bit_extender_4_out,
       multiplier_1_out, multiplier_2_out;
  wire [7:0] counter_2_q, counter_3_q, rom_1_data, rom_2_data, undriven;

  ROM #(.addrWidth(7)) rom_1 (.addr(charIn), .data(rom_1_data));
  and and_1 (and_1_out, muxt, ~and_3_out);  // AND_Gate
  and and_2 (and_2_out, counter_4_carry, ~comparator_1_eq);  // AND_Gate
  Comparator comparator_1 (.a(counter_2_q), .b(8'h7), .eq(comparator_1_eq));  // open: gt, lt
  Counter #(.max('h7), .width(3)) counter_1 (
    .count(and_1_out), .Q(counter_1_q), .clk(CLK), .clr(reset));  // open: load, D, carry, up
  Counter counter_2 (.count(and_2_out), .Q(counter_2_q), .clk(CLK), .clr(reset));  // open: load, D, carry, up
  Decoder #(.select(3)) decoder_1 (
    .out0(decoder_1_out0), .out1(decoder_1_out1), .out2(decoder_1_out2), .out3(decoder_1_out3),
    .out4(decoder_1_out4), .sel(counter_1_q));  // open: out5, out6, out7, en
  and and_3 (and_3_out, decoder_1_out2, ~counter_5_carry);  // AND_Gate
  ROM rom_2 (.addr(counter_2_q), .data(rom_2_data));
  and and_4 (muxt, drawChar, ~decoder_1_out4);  // AND_Gate
  not not_1 (cx_clear, muxt);
  Counter counter_3 (.count(decoder_1_out3), .Q(counter_3_q), .clk(CLK));  // open: load, D, carry, up, clr
  or or_1 (or_1_out, decoder_1_out1, decoder_1_out2);
  // XOR_Gate xor_1 has open pins: in0={8{1'b1}}, in1=undriven, out=open
  assign bit_extender_1_out = {{3{1'b0}}, counter_3_q[3:0]};  // Bit_Extender bit_extender_1
  assign bit_extender_2_out = {{3{1'b0}}, counter_3_q[7:4]};  // Bit_Extender bit_extender_2
  Multiplier #(.width(7)) multiplier_1 (
    .a(7'b0001000), .b(bit_extender_1_out), .out(multiplier_1_out));  // open: cin, cout
  Multiplier #(.width(7)) multiplier_2 (
    .a(7'b0001000), .b(bit_extender_2_out), .out(multiplier_2_out));  // open: cin, cout
  BitSelector bitselector_1 (
    .in({rom_2_data[0], rom_2_data[1], rom_2_data[2], rom_2_data[3], rom_2_data[4], rom_2_data[5], rom_2_data[6], rom_2_data[7]}),
    .out(bitselector_1_out), .sel(counter_4_q));
  Counter #(.max('h7), .width(3)) counter_4 (
    .count(or_1_out), .Q(counter_4_q), .carry(counter_4_carry), .clk(CLK), .clr(decoder_1_out0));  // open: load, D, up
  assign Color = muxt ? controlled_buffer_2_out : 3'bz;  // Controlled_Buffer controlled_buffer_1
  not not_2 (not_2_out, bitselector_1_out);
  assign bit_extender_3_out = {{4{1'b0}}, counter_4_q};  // Bit_Extender bit_extender_3
  Counter #(.max('h7), .width(3)) counter_5 (
    .count(counter_4_carry), .Q(counter_5_q), .carry(counter_5_carry), .clk(CLK), .clr(decoder_1_out0));  // open: load, D, up
  assign controlled_buffer_2_out = bitselector_1_out ? color_a : 3'bz;  // Controlled_Buffer controlled_buffer_2
  Hex_Digit_Display hex_digit_display_1 (.value({undriven_2, posxy[5:4]}));  // open: dp
  Hex_Digit_Display hex_digit_display_2 (.value(posxy[3:0]));  // open: dp
  Adder #(.width(7)) adder_1 (.a(multiplier_1_out), .b(bit_extender_3_out), .out(posxy[6:0]));  // open: cin, cout
  assign bit_extender_4_out = {{4{1'b0}}, counter_5_q};  // Bit_Extender bit_extender_4
  assign controlled_buffer_2_out = not_2_out ? color_b : 3'bz;  // Controlled_Buffer controlled_buffer_3
  Adder #(.width(7)) adder_2 (.a(bit_extender_4_out), .b(multiplier_2_out), .out(posxy[13:7]));  // open: cin, cout
  Hex_Digit_Display hex_digit_display_3 (.value({undriven_3, posxy[12:11]}));  // open: dp
  Hex_Digit_Display hex_digit_display_4 (.value(posxy[10:7]));  // open: dp

  // Notes on the sheet:
  //   contents of rom_2 (hex, n*v repeats v):
  //   7c 82 82 fe 82 82 82 0 fc 82 82 8c 82 82 fc
endmodule
